# Fritzing sketch stm32-adc-am2302 (saved by Fritzing 1.0.0rc)

parts:
  J1 = STM32 Nucleo boards
  AM1 = AM2302 Humidity and Temperature Sensor

nets:
  N1: J1.D2, AM1.DATA
  3V3: J1.3V3, AM1.VDD
  GND: J1.GND, AM1.GND
